// Digital circuit cpu_proc16b2.dig as structural Verilog
module cpu_proc16b2 (
  input  [15:0] inst,
  input  [15:0] bus_in,
  input  clock,
  output [15:0] ptr_inst,
  output [15:0] bus_addr,
  output [15:0] bus_out,
  output bus_write,
  output \break 
);

  wire and_1_out, jump_cmp, jump_success, mode_alu, mode_jump, write_overflow;
  wire [1:0] jump_x, jump_y;
  wire [3:0] decoder_1_addr_sel, decoder_1_d_sel, decoder_1_x_sel, decoder_1_y_sel, decoder_1_z_sel;
  wire [15:0] add_1_s, addr, alu_operands_1_x, alu_operands_1_y, d, decoder_1_constant, reg_a, reg_b, reg_c,
       reg_d, reg_flags, reg_pc, reg_rem, write_pc, write_remainder, write_val, x, y, z;

  decoder decoder_1 (
    .instruction(inst), .constant(decoder_1_constant), .addr_sel(decoder_1_addr_sel),
    .X_sel(decoder_1_x_sel), .Y_sel(decoder_1_y_sel), .Z_sel(decoder_1_z_sel), .D_sel(decoder_1_d_sel));  // open: O_sel, OP, brk
  Register #(.Bits(16)) A (.D(write_val), .C(clock), .Q(reg_a));  // open: en
  Register #(.Bits(16)) B (.D(write_val), .C(clock), .Q(reg_b));  // open: en
  Register #(.Bits(16)) C (.D(write_val), .C(clock), .Q(reg_c));  // open: en
  Register #(.Bits(16)) u_D (.D(write_val), .C(clock), .Q(reg_d));  // open: en
  Register #(.Bits(16)) flags (.D({{15{1'b0}}, write_overflow}), .C(clock), .en(mode_alu), .Q(reg_flags));
  Register #(.Bits(16)) r (.D(write_remainder), .C(clock), .en(mode_alu), .Q(reg_rem));
  // Probe reg_a on reg_a
  // Probe reg_b on reg_b
  // Probe reg_c on reg_c
  // Probe reg_d on reg_d
  // Probe reg_flags on reg_flags
  // Probe reg_r on reg_rem
  operand_selector operand_selector_1 (
    .reg_A(reg_a), .reg_B(reg_b), .reg_C(reg_c), .reg_D(reg_d), .reg_rem(reg_rem), .reg_flags(reg_flags),
    .ALU(reg_pc), .bus(bus_in), .constant(decoder_1_constant), .X_sel(decoder_1_x_sel),
    .Y_sel(decoder_1_y_sel), .Z_sel(decoder_1_z_sel), .D_sel(decoder_1_d_sel), .addr_sel(decoder_1_addr_sel),
    .X(x), .Y(y), .D(d), .Z(z), .addr(addr));  // open: jump, PC
  alu alu_1 ();  // open: opcode, X, Y, Z, remainder, overflow
  alu_operands alu_operands_1 (
    .Xsel(jump_x), .Ysel(jump_y), .a(reg_a), .b(reg_b), .c(reg_c), .d(reg_d), .X(alu_operands_1_x),
    .Y(alu_operands_1_y));
  Add #(.Bits(16)) add_1 (.a(reg_pc), .b(16'h1), .c_i(1'b0), .s(add_1_s));  // open: c_o
  Register #(.Bits(16), .isProgramCounter("true")) PC (.D(write_pc), .C(clock), .en(1'b1), .Q(reg_pc));
  and and_1 (and_1_out, mode_jump, jump_success);
  // Probe reg_pc on reg_pc
  Multiplexer #(.Bits(16)) multiplexer_1 (.sel(and_1_out), .in_0(add_1_s), .out(write_pc));  // open: in_1
  // compare compare_1: pin names not known; wires that end beside it: alu_operands_1_x, alu_operands_1_y, jump_cmp, jump_success

  // Notes on the sheet:
  //   input decoder/control unit
  //   output
  //   jump controller
  //   program counter
  //   jump
endmodule

/* Test case ldc tests:
clock inst  bus_in  reg_a  reg_b  reg_c  reg_d  reg_o  reg_r
C  0b0000000000000001  0   1  0  0  0  0  0
C  0b0000000000000010  0   2  0  0  0  0  0
C  0b0001000000000011  0   2  3  0  0  0  0
C  0b0010000000000100  0   2  3  4  0  0  0
C  0b0011000000000101  0   2  3  4  5  0  0
*/

/* Test case alu tests:
clock inst  reg_a  reg_b  reg_c  reg_d  reg_r
# ldc %a, $1
C  0b0000000000000001  1  0  0  0  x
# ldc %b, $2
C  0b0001000000000010  1  2  0  0  x

# add %c, %a, %b
#    01xxyywwooooo___
C  0b0100011000000000  1  2  3  0  x

# sub %c, %b, %a
C  0b0101001000001000  1  2  1  0  x

# div %c, %a, %b
C  0b0100011000011000  1  2  0  0  1
*/

/* Test case jump tests:
clock  inst  reg_a  reg_b  reg_c  reg_d  reg_pc

# note: clock/reg_pc weirdness
# if you use a C signal in Digital, it first sets all the inputs, then pulses the clock, and then compares the outputs.
# the result of this is that the reg_pc probe is always the instruction pointer that the cpu wants NEXT.
# so, if you run the first test line and pulse the clock right away, reg_pc should be 1. it was 0 before the clock pulse.
# but if you execute a jump to 0, then the reg_pc will be 0. because that's the instruction that it wants next.
# it's a little unintuitive to me. maybe it isn't to you.

# ldc %a, $1
#    00rrvvvvvvvvvvvv
C  0b0000000000000001  1  0  0  0  1

# ldc %b, $2
C  0b0001000000000010  1  2  0  0  2

# ldc %d, $0xFF
C  0b0011000011111111  1  2  0  0xFF 3

# jgt %c, %a, %b (jump to c if a > b) (it's not)
#    100xxyyttccc____
C  0b1000001100010000  1  2  0  0xFF  4

# jlt %c, %a, %b (jump to c if a < b) (it is)
#    100xxyyttccc____
C  0b1000001101000000  1  2  0  0xFF  0

# jlt %d, %a, %b (jump to d if a < b) (it is)
#    100xxyyttccc____
C  0b1000001111000000  1  2  0  0xFF  0xFF

# jump to c if false
#    100xxyyttccc____
C  0b1000001100000000  1  2  0  0xFF  0x100

# jmp %c (jump to c if true)
#    100xxyyttccc____
C  0b1000001101110000  1  2  0  0xFF  0
*/

/* Test case rw tests:
clock  inst          bus_in  reg_a  reg_b  reg_c  reg_d  reg_o  reg_r  bus_write  bus_addr  bus_out

# set up some values in registers
# o=0, r=1, a=2, b=3, c=4, d=5

# ldc %a, $2
C 0b0000000000000010 0x0000  0x0002 0x0000 0x0000 0x0000 0x0000 0x0000 0 x      x
# ldc %b, $3
C 0b0001000000000011 0x0000  0x0002 0x0003 0x0000 0x0000 0x0000 0x0000 0 x      x
# ldc %c, $4
C 0b0010000000000100 0x0000  0x0002 0x0003 0x0004 0x0000 0x0000 0x0000 0 x      x
# ldc %d, $5
C 0b0011000000000101 0x0000  0x0002 0x0003 0x0004 0x0005 0x0000 0x0000 0 x      x
# div %a, %d, %a (a = 5 / 2) a = 2, r = 1
#   01xxyywwooooo___
C 0b0111000000011000 0x0000  0x0002 0x0003 0x0004 0x0005 0x0000 0x0001 0 x      x

# stb %a, %b (*a = b)
#   1011maaavvv_____
C 0b1011100000100000 0x0000  0x0002 0x0003 0x0004 0x0005 0x0000 0x0001 1 0x0002 0x0003

# stb %c, %d (*c = d)
C 0b1011101001100000 0x0000  0x0002 0x0003 0x0004 0x0005 0x0000 0x0001 1 0x0004 0x0005

# ldb %a, %b (b = *a)
C 0b1011000000100000 0x0006  0x0002 0x0006 0x0004 0x0005 0x0000 0x0001 0 0x0002 x

# ldb %c, %a (a = *c)
C 0b1011001000000000 0x0007  0x0007 0x0006 0x0004 0x0005 0x0000 0x0001 0 0x0004 x
*/

/* Test case misc tests:
clock  inst  ptr_inst  bus_write  break
# noop
#   111_----____----
0 0b1110000000000000 0  0  0
# brk
C 0b1110000000000001 1  0  1
C 0b1110000000000000 2  0  0
C 0b1110000000000001 3  0  1
*/

/* Test case ramfill test:
clock inst            reg_a  reg_b  reg_c  reg_d  ptr_inst bus_addr bus_out bus_write
C 0b0000000000000000  0x0000 0x0000 0x0000 0x0000 0x0001   x        x       0
C 0b0001000000000000  0x0000 0x0000 0x0000 0x0000 0x0002   x        x       0
C 0b0010000000000001  0x0000 0x0000 0x0001 0x0000 0x0003   x        x       0

# loop block
C 0b0011000000000010  0x0000 0x0000 0x0001 0x0002 0x0004   x        x       0
C 0b0100100000000000  0x0001 0x0000 0x0001 0x0002 0x0005   x        x       0
C 0b0100110100010000  0x0001 0x0002 0x0001 0x0002 0x0006   x        x       0
C 0b1011100000100000  0x0001 0x0002 0x0001 0x0002 0x0007   0x0001   0x0002  1
C 0b0011000000000011  0x0001 0x0002 0x0001 0x0003 0x0008   x        x       0
C 0b1000000111110000  0x0001 0x0002 0x0001 0x0003 0x0003   x        x       0

# see note in "jump tests"
C 0b0011000000000010  0x0001 0x0002 0x0001 0x0002 0x0004   x        x       0
C 0b0100100000000000  0x0002 0x0002 0x0001 0x0002 0x0005   x        x       0
C 0b0100110100010000  0x0002 0x0004 0x0001 0x0002 0x0006   x        x       0
C 0b1011100000100000  0x0002 0x0004 0x0001 0x0002 0x0007   0x0002   0x0004  1
C 0b0011000000000011  0x0002 0x0004 0x0001 0x0003 0x0008   x        x       0
C 0b1000000111110000  0x0002 0x0004 0x0001 0x0003 0x0003   x        x       0


C 0b0011000000000010  0x0002 0x0004 0x0001 0x0002 0x0004   x        x       0
C 0b0100100000000000  0x0003 0x0004 0x0001 0x0002 0x0005   x        x       0
C 0b0100110100010000  0x0003 0x0006 0x0001 0x0002 0x0006   x        x       0
C 0b1011100000100000  0x0003 0x0006 0x0001 0x0002 0x0007   0x0003   0x0006  1
C 0b0011000000000011  0x0003 0x0006 0x0001 0x0003 0x0008   x        x       0
C 0b1000000111110000  0x0003 0x0006 0x0001 0x0003 0x0003   x        x       0


C 0b0011000000000010  0x0003 0x0006 0x0001 0x0002 0x0004   x        x       0
C 0b0100100000000000  0x0004 0x0006 0x0001 0x0002 0x0005   x        x       0
C 0b0100110100010000  0x0004 0x0008 0x0001 0x0002 0x0006   x        x       0
C 0b1011100000100000  0x0004 0x0008 0x0001 0x0002 0x0007   0x0004   0x0008  1
C 0b0011000000000011  0x0004 0x0008 0x0001 0x0003 0x0008   x        x       0
C 0b1000000111110000  0x0004 0x0008 0x0001 0x0003 0x0003   x        x       0
*/

/* Test case increment test:
clock inst            reg_a  reg_b  reg_c  reg_d  ptr_inst bus_write
C 0b0000000000000000  0x0000 0x0000 0x0000 0x0000 0x0001   0
C 0b0001000000000001  0x0000 0x0001 0x0000 0x0000 0x0002   0
C 0b0010000000000011  0x0000 0x0001 0x0003 0x0000 0x0003   0

C 0b0100010000000000  0x0001 0x0001 0x0003 0x0000 0x0004   0
C 0b1000000101110000  0x0001 0x0001 0x0003 0x0000 0x0003   0

C 0b0100010000000000  0x0002 0x0001 0x0003 0x0000 0x0004   0
C 0b1000000101110000  0x0002 0x0001 0x0003 0x0000 0x0003   0

C 0b0100010000000000  0x0003 0x0001 0x0003 0x0000 0x0004   0
C 0b1000000101110000  0x0003 0x0001 0x0003 0x0000 0x0003   0

C 0b0100010000000000  0x0004 0x0001 0x0003 0x0000 0x0004   0
C 0b1000000101110000  0x0004 0x0001 0x0003 0x0000 0x0003   0

C 0b0100010000000000  0x0005 0x0001 0x0003 0x0000 0x0004   0
C 0b1000000101110000  0x0005 0x0001 0x0003 0x0000 0x0003   0

C 0b0100010000000000  0x0006 0x0001 0x0003 0x0000 0x0004   0
C 0b1000000101110000  0x0006 0x0001 0x0003 0x0000 0x0003   0

C 0b0100010000000000  0x0007 0x0001 0x0003 0x0000 0x0004   0
C 0b1000000101110000  0x0007 0x0001 0x0003 0x0000 0x0003   0
*/

/* Test case fibonacci tests:
clock inst bus_in  reg_a  reg_b  reg_c  reg_d  ptr_inst bus_addr bus_out bus_write
C   0x0001 0xFFFF  0x0001 x      x      x      0x0001   x        x       0
C   0xb800 0xFFFF  0x0001 x      x      x      0x0002   0x0001   0x0001  1
C   0x0002 0xFFFF  0x0002 x      x      x      0x0003   x        x       0
C   0xb800 0xFFFF  0x0002 x      x      x      0x0004   0x0002   0x0002  1
C   0x1000 0xFFFF  0x0002 0x0000 x      x      0x0005   x        x       0
C   0xb900 0xFFFF  0x0002 0x0000 x      x      0x0006   0x0000   0x0002  1
C   0x0001 0xFFFF  0x0001 0x0000 x      x      0x0007   x        x       0
C   0x3001 0xFFFF  0x0001 0x0000 x      0x0001 0x0008   x        x       0
#C   0xb360 0x0000  0x0001 0x0000 x      0x0001 0x0009   0x0001   x       0
*/

/* Test case short regression 1:
# 0xA100 was found to be able to cause a short. however, it is a legal instruction.
# this is non deterministic.
# adding repeated 0xA100 instructions does not seem to increase the chance of it happening,
# but resetting the registers every time does.

clock inst  reg_a  reg_b

loop(a,10)
  C  0x0000   0      x
  C  0x1004   0      4
  C  0xA100   4      4
end loop
*/
