// Digital circuit cpu_proc16b1.dig as structural Verilog
module cpu_proc16b1 (
  input  [15:0] instruction,
  input  bus_in,
  input  clock
);

  wire alu_operands_1_p1, alu_operands_1_p2, read_a, read_b, read_bus, read_c, read_d, read_o, read_r,
       write_a, write_b, write_bus, write_c, write_d;
  wire [1:0] alu_x, alu_y, jump_tgt, jump_x, jump_y;
  wire [2:0] bus_address, jump_cmp, mode;
  wire [4:0] alu_op;
  wire [15:0] constant_value, write_val;

  decoder decoder_1 (
    .instruction(instruction), .mode(mode), .constant_value(constant_value), .alu_x(alu_x), .alu_y(alu_y),
    .alu_op(alu_op), .jump_x(jump_x), .jump_y(jump_y), .jump_tgt(jump_tgt), .jump_cmp(jump_cmp),
    .bus_address(bus_address), .read_a(read_a), .read_b(read_b), .read_c(read_c), .read_d(read_d),
    .read_bus(read_bus), .read_o(read_o), .read_r(read_r), .write_a(write_a), .write_b(write_b),
    .write_c(write_c), .write_d(write_d), .write_bus(write_bus));
  Register #(.Bits(16)) A (.D(write_val), .C(clock), .en(write_a));  // open: Q
  Register #(.Bits(16)) B (.D(write_val), .C(clock), .en(write_b));  // open: Q
  Register #(.Bits(16)) C (.D(write_val), .C(clock), .en(write_c));  // open: Q
  Register #(.Bits(16)) D (.D(write_val), .C(clock), .en(write_d));  // open: Q
  Register #(.Bits(16)) o (.C(clock));  // open: D, en, Q
  Register #(.Bits(16)) r (.C(clock));  // open: D, en, Q
  // alu_operands alu_operands_1: pin names not known; wires that end beside it: alu_operands_1_p1, alu_operands_1_p2
  // alu alu_1: pin names not known; wires that end beside it: alu_operands_1_p1, alu_operands_1_p2
endmodule
